# Fritzing sketch ThroughHoleProtoType (saved by Fritzing 0.9.10b)
breadboards: 1

parts:
  Part1 = Adafruit Feather nRF52840 [part_number=4062]
  Part2 = OLED Monochrome 128x64 0.96 inch [part_number=326]
  IR_Recv = TSOP312.., 314.. [package=THT]
  Adafruit_High_Power_Infrared_LED_Emitter1 = Adafruit High Power Infrared LED Emitter - STEMMA JST PH 2mm [part_number=#5639]
  S1 = JOYSTICK_MINI [package=joystick_mini]

nets:
  VIN: Part1.3.3V, Part2.VIN, IR_Recv.Vs, Adafruit_High_Power_Infrared_LED_Emitter1.VIN
  GND: Part1.GND, Part2.GND, IR_Recv.GND, Adafruit_High_Power_Infrared_LED_Emitter1.GND, S1.GND
  N1: Part1.SDA, Part2.MOSI_SDA
  N2: Part1.SCL, Part2.SCLK_SCK
  N3: Part1.D5, S1.CENT
  N4: Part1.D6, S1.DOWN
  N5: Part1.D9, S1.LEFT
  N6: Part1.D10, S1.RIGHT
  N7: Part1.D11, S1.UP
  N8: Part1.D12, IR_Recv.Data
  N9: Part1.D13, Adafruit_High_Power_Infrared_LED_Emitter1.SIGNAL

custom parts:
  Adafruit Feather nRF52840: The Adafruit Feather nRF52840 Express is our take on an 'all-in-one' Arduino-compatible + Bluetooth Low Energy with built in USB plus battery charging, 1 MB of FLASH and 256KB of SRAM. With native USB it's even ready to join the CircuitPython party. For this chip, we've added Arduino IDE support - you can program the nRF52840 chip directly to take full advantage of the Cortex-M4 processor, and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
  OLED Monochrome 128x64 0.96 inch: These displays are small, only about 1" diameter, but very readable due to the high contrast of an OLED display. This display is made of 128x64 individual white OLED pixels, each one is turned on or off by the controller chip. Because the display makes its own light, no backlight is required. This reduces the power required to run the OLED and is why the display has such high contrast; we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
  Adafruit High Power Infrared LED Emitter - STEMMA JST PH 2mm: *pew* *pew*! This board is like a little ray gun for infrared light, with two high powered LED outputs. When controlled with the onboard N-Channel FET driver, you'll be blasting 100mA-200mA of current pulsing through each LED for 10+ meters of range! This is the easiest way to get great IR emitter range without wiring up a bunch of parts. By using a 2mm pitch STEMMA JST PH cable with headers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
